# Fritzing sketch esp-201-board (saved by Fritzing 0.9.2b)
circuit board: 9cm x 7cm
perfboards: 1

parts:
  S1 = Pushbutton [package="[THT]"]
  S2 = Toggle Switch [package=THT]
  R1 = Resistor [tolerance=±5% resistance=4.7k package=THT]
  U1 = ESP8266 WiFi Module [part_number=ESP8266]
  U2 = Voltage Regulator - 3.3V [package="TO220 [THT]"]
  C1 = Electrolytic Capacitor [capacitance=33µF voltage=50V package="100 mil [THT, electrolytic]"]
  C2 = Electrolytic Capacitor [capacitance=0.47µF voltage=50V package="100 mil [THT, electrolytic]"]
  J1 = female pin header, 3 pins [form="♀ (female)"]
  J2 = female pin header, 3 pins [form="♀ (female)"]
  C3 = Electrolytic Capacitor [capacitance=680µF voltage=25V package="100 mil [THT, electrolytic]"]
  C4 = Ceramic Capacitor [capacitance=100nF package="100 mil [THT, multilayer]"]
  R2 = Resistor [tolerance=±5% resistance=4.7k package=THT]
  R3 = Resistor [tolerance=±5% resistance=4.7k package=THT]
  J3 = female pin header, 3 pins [form="♀ (female)"]
  J4 = female pin header, 3 pins [form="♀ (female)"]
  J5 = female pin header, 3 pins [form="♀ (female)"]
  J6 = female pin header, 3 pins [form="♀ (female)"]
  R4 = Resistor [tolerance=±5% resistance=3.3k package=THT]
  R5 = Resistor [tolerance=±5% resistance=3.3k package=THT]
  R6 = Resistor [tolerance=±5% resistance=3.3k package=THT]
  R7 = Resistor [tolerance=±5% resistance=3.3k package=THT]

nets:
  N1: S1.Pin_1, S1.Pin_2, S2.L2, U1.GND#12, U1.GND#13, U1.IO15, U2.GND, C1.-, C2.-, J1.pin2, C3.-, C4.1, J3.pin3, J4.pin3, J5.pin3, J6.pin3
  N2: S1.Pin_3, S1.Pin_4, U1.RST, R2.Pin_0
  N3: S2.L1, R3.Pin_0
  N4: S2.COM, U1.IO0
  N5: R1.Pin_0, U1.CHIP_EN
  N6: R1.Pin_1, U1.3.3V#10, U1.3.3V#11, U2.output_voltage, C1.+, C3.+, C4.0, R2.Pin_1, R3.Pin_1, J3.pin1, J4.pin1, J5.pin1, J6.pin1, R4.Pin_0, R5.Pin_0, R6.Pin_0, R7.Pin_0
  N7: U1.IO5, J6.pin2, R4.Pin_1
  N8: U1.IO14, J5.pin2, R5.Pin_1
  N9: U1.IO12, J4.pin2, R6.Pin_1
  N10: U1.IO13, J3.pin2, R7.Pin_1
  N11: U1.GND#23, J2.pin1
  N12: U1.TX, J2.pin2
  N13: U1.RX, J2.pin3
  N14: U2.input_voltage, C2.+, J1.pin1
